# Fritzing sketch Automated_Dustbin_Project (saved by Fritzing 0.9.4)
circuit board: 1.59177cm x 1.98396cm
circuit board: 1.08676cm x 1.42015cm
circuit board: 4.79515cm x 2.19782cm
circuit board: 7.36481cm x 6.28096cm
breadboards: 1

parts:
  S1 = Pushbutton [package="[THT]"]
  J1 = Basic Servo
  HC-SR04_Sensor_1 = HC-SR04 Ultrasonic Distance Sensor
  R2 = Resistor [tolerance=±5% resistance=1k package=THT]
  LED1 = RGB LED (com. cathode, rgb) [package="5 mm [THT]"]
  Part2 = HC-SR501 Body Sensor Module
  J2 = Dagu DGServo 9g header (male) [package=THT]
  J3 = Dagu DGServo 9g header (male) [package=THT]
  J4 = Dagu DGServo 9g header (male) [package=THT]
  J5 = Dagu DGServo 9g header (male) [package=THT]
  J9 = Dagu DGServo 9g header (male) [package=THT]
  J10 = Dagu DGServo 9g header (male) [package=THT]
  J11 = Dagu DGServo 9g header (male) [package=THT]
  Part1 = Arduino Uno (Rev3)
  J12 = Dagu DGServo 9g header (male) [package=THT]

nets:
  N1: S1.Pin_1, S1.Pin_2, R2.Pin_1, LED1.common_cathode, Part1.D11_PWM/MOSI
  VCC: S1.Pin_3, S1.Pin_4, J1.vcc, HC-SR04_Sensor_1.VCC, Part2.VCC, J2.Vcc, J3.Vcc, J4.Vcc, J9.Vcc, J10.Vcc, J11.Vcc, Part1.5V
  GND: J1.gnd, HC-SR04_Sensor_1.GND, R2.Pin_0, Part2.GND, J2.gnd, J3.gnd, J4.gnd, J9.gnd, J10.gnd, J11.gnd, Part1.GND
  N2: J1.pulse, J3.pulse, J11.pulse, Part1.D6_PWM
  N3: HC-SR04_Sensor_1.TRIG, J5.Vcc, Part1.D9_PWM, J12.pulse
  N4: HC-SR04_Sensor_1.ECHO, J5.pulse, Part1.D8, J12.Vcc
  N5: LED1.red_anode, Part1.D4
  N6: LED1.green_anode, Part1.D2
  N7: LED1.blue_anode, Part1.D3_PWM
  N8: Part2.OUT, J2.pulse, J10.pulse, Part1.D13/SCK

custom parts:
  HC-SR501 Body Sensor Module: Pyroelectric Infrared PIR Motion Sensor Detector Module

// code stored in the sketch: try.ino

#include <Servo.h>

int servoPos = 0;

Servo servo_9;
#define pirPin 13
#define trigPin 9
#define echoPin 8
#define overridePin 11

#define greenPin 2
#define yellowPin 3
#define redPin 4

long duration;
int distance;
int pirState = LOW;
int val = 0;

void setup() {
  servo_9.attach(6, 500, 2500);
  pinMode(pirPin, INPUT);
  pinMode(trigPin, OUTPUT);
  pinMode(echoPin, INPUT);
  pinMode(overridePin, INPUT);
  
  pinMode(greenPin, OUTPUT);
  pinMode(yellowPin, OUTPUT);
  pinMode(redPin, OUTPUT);
 
}

void loop() {
  checkDistance();
  checkPIR();
  checkOverride();
  checkBinStatus();
}

void checkDistance() {
  digitalWrite(trigPin, LOW);
  delayMicroseconds(2);
  digitalWrite(trigPin, HIGH);
  delayMicroseconds(10);
  digitalWrite(trigPin, LOW);

  duration = pulseIn(echoPin, HIGH);
  distance = duration * 0.034 / 2;
}

void checkPIR() {
  if (digitalRead(pirPin) == HIGH) {
    openLid();
    pirState = HIGH;
  
  }
  if (pirState == HIGH) {
    closeLid();
    pirState = LOW;
  }
}

void checkOverride() {
  if (digitalRead(overridePin) == HIGH) {
    openLid();
    closeLid();
  }
}

void checkBinStatus() {
  int binLevel = map(distance, 0, 200, 0, 100);
  
  if (binLevel < 40) {
    setColor(1, 0, 0); 
  } else if (binLevel >= 40 && binLevel < 70) {
    setColor(1, 1, 0);
  } else {
    setColor(0, 1, 0); 
  }
}

void openLid() {
  for (servoPos = 0; servoPos <= 90; servoPos += 1) {
    servo_9.write(servoPos);
    delay(15);
  }
  delay(5000);
}

void closeLid() {
  for (servoPos = 90; servoPos >= 0; servoPos -= 1) {
    servo_9.write(servoPos);
    delay(15); 
  }
  delay(5000);
}

void setColor(int red, int green, int blue) {
  digitalWrite(redPin, red);
  digitalWrite(greenPin, green);
  digitalWrite(yellowPin, blue);
}
